# Fritzing sketch Bekant (saved by Fritzing 0.9.3b)
breadboards: 1

parts:
  Part1 = Arduino Uno (Rev3)
  U1 = MCP2003B [part_number=MCP2003B chip_label=U1 package=8-SOIC]
  R1 = Resistor [tolerance=±5% resistance=2.2k package=THT]
  R2 = Resistor [tolerance=±5% resistance=2.2k package=THT]
  R3 = Resistor [tolerance=±5% resistance=2.2k package=THT]
  R4 = Resistor [tolerance=±5% resistance=1k package=THT]
  S1_(UP) = Pushbutton [package="[THT]"]
  S2_(DOWN) = Pushbutton [package="[THT]"]

nets:
  N1: Part1.D8, S2_(DOWN).Pin_3, S2_(DOWN).Pin_4
  N2: Part1.D0/RX, U1.RxD, R1.Pin_0
  N3: Part1.D1/TX, U1.TxD
  N4: Part1.D7, S1_(UP).Pin_3, S1_(UP).Pin_4
  N5: Part1.5V, R1.Pin_1, R2.Pin_1
  GND/LIN Ground (pin 2): Part1.GND, U1.Vss, R3.Pin_1, S1_(UP).Pin_1, S1_(UP).Pin_2, S2_(DOWN).Pin_1, S2_(DOWN).Pin_2
  12V: Part1.VIN, U1.Vbb, R4.Pin_1
  N6: U1.CS, R2.Pin_0
  N7: U1.!WAKE, R3.Pin_0
  LIN bus (pin 3): U1.Lbus, R4.Pin_0

notes:
  LIN Bus (pin 3)
  LIN Ground (pin 2)
  12V Supply

custom parts:
  MCP2003B: LIN Transciever
